# Fritzing sketch Wiring (saved by Fritzing 0.9.3b)
breadboards: 1

parts:
  Bauteil1 = Arduino Uno (Rev3) - ICSP
  Bauteil2 = Triple Axis Accelerometer Breakout - ADXL345
  Bauteil3 = Adafruit DRV2605L [part_number="Adafruit #2305"]
  Bauteil4 = 24 NeoPixel Ring [part_number=1586]
  Bauteil5 = 12 NeoPixel Ring [part_number=1643]

nets:
  N1: Bauteil1.A4/SDA, Bauteil2.SDA, Bauteil3.SDA
  N2: Bauteil1.A5/SCL, Bauteil2.SCL, Bauteil3.SCL
  N3: Bauteil1.D8, Bauteil4.IN
  N4: Bauteil1.D9_PWM, Bauteil5.IN
  N5: Bauteil1.D2, Bauteil2.INT1
  5V: Bauteil1.5V, Bauteil2.VCC, Bauteil3.VIN, Bauteil5.VDD
  GND: Bauteil1.GND, Bauteil2.GND, Bauteil3.GND, Bauteil4.GND, Bauteil5.GND

custom parts:
  Adafruit DRV2605L: The DRV2605 from TI is a fancy little motor driver. Rather than controlling a stepper motor or DC motor, its designed specifically for controlling haptic motors - buzzers and vibration motors. Normally one would just turn those kinds of motors on and off, but this driver has the ability to have various effects when driving a vibe motor. For example, ramping the vibration level up and down,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
  24 NeoPixel Ring: 24 ultra bright smart LED NeoPixels are arranged in a circle with 2.6" (66mm) outer diameter. The rings are 'chainable' - connect the output pin of one to the input pin of another. Use only one microcontroller pin to control as many as you can chain together! Each LED is addressable as the driver chip is inside the LED. Each one has ~18mA constant current drive so the color will be very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
  12 NeoPixel Ring: 12 ultra bright smart LED NeoPixels are arranged in a circle with 1.5" (37mm) outer diameter. The rings are 'chainable' - connect the output pin of one to the input pin of another. Use only one microcontroller pin to control as many as you can chain together! Each LED is addressable as the driver chip is inside the LED. Each one has ~18mA constant current drive so the color will be very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
